// Logisim project cpu.circ as structural Verilog: 3 circuits, main circuit datapath
module ALU (
  input  [7:0] A,
  input  [7:0] B,
  input  [2:0] S,
  output [7:0] Out,
  output ZF,
  output VF
);

  wire A7, A_B, A_B_t, and_6_out, and_7_out, B7, Inc_A, Inc_B, not_5_out, not_6_out, not_7_out, Not_S0,
       Not_S1, Not_S2, or_2_out, or_3_out, R7;
  wire [6:0] adder_1_out, multiplexer_1_out, multiplexer_2_out;
  wire [7:0] and_3_out, multiplexer_3_out, not_1_out, or_1_out;

  assign not_1_out = ~B;  // NOT_Gate not_1, 8 bits wide
  and and_1 (Inc_A, Not_S2, S[1], Not_S0);
  and and_2 (Inc_B, Not_S2, S[1], S[0]);
  Multiplexer #(.width(8), .enable("false")) multiplexer_1 (
    .in0(A), .in1(8'h1), .out({A7, multiplexer_1_out}), .sel(Inc_B));
  Multiplexer #(.width(8), .enable("false")) multiplexer_2 (
    .in0(multiplexer_3_out), .in1(not_1_out), .out({B7, multiplexer_2_out}), .sel(A_B_t));
  Multiplexer #(.width(8), .enable("false")) multiplexer_3 (.in0(B), .in1(8'h1), .out(multiplexer_3_out), .sel(Inc_A));
  assign and_3_out = A & B;  // AND_Gate and_3, 8 bits wide
  assign or_1_out = A | B;  // OR_Gate or_1, 8 bits wide
  Adder adder_1 (
    .a({A7, multiplexer_1_out}), .b({B7, multiplexer_2_out}), .out({R7, adder_1_out}), .cin(A_B_t));  // open: cout
  not not_2 (Not_S0, S[0]);
  not not_3 (Not_S1, S[1]);
  not not_4 (Not_S2, S[2]);
  and and_4 (A_B, S[2], Not_S1, Not_S0);
  and and_5 (A_B_t, S[2], Not_S1, S[0]);
  Multiplexer #(.select(3), .width(8), .enable("false")) multiplexer_4 (
    .in0(A), .in1(B), .in2({R7, adder_1_out}), .in3({R7, adder_1_out}), .in4({R7, adder_1_out}),
    .in5({R7, adder_1_out}), .in6(and_3_out), .in7(or_1_out), .out(Out), .sel(S));
  not not_5 (not_5_out, A7);
  not not_6 (not_6_out, B7);
  not not_7 (not_7_out, R7);
  and and_6 (and_6_out, not_5_out, R7, not_6_out);
  and and_7 (and_7_out, A7, not_7_out, B7);
  nor nor_1 (ZF, Out[0], Out[1], Out[2], Out[3], Out[4], Out[5], Out[6], Out[7]);
  or or_2 (or_2_out, and_6_out, and_7_out);
  or or_3 (or_3_out, Inc_A, Inc_B, A_B, A_B_t);
  and and_8 (VF, or_2_out, or_3_out);

  // Notes on the sheet:
  //   Opcode Detectors - used to detect which arithmetic op we are performing
  //   Extract MSB of operands
  //   and result for overflow
  //   detection.
  //   8-bit ALU with zero and overflow detection
  //   Author: RR
  //   Logic for VF: We performed addition,
  //   increment, or subtraction and there was a sign
  //   mismatch between operands and result
endmodule

module datapath (
  input  [7:0] Input,
  input  RST,
  output halt,
  output [7:0] Out
);

  wire A_Enable, B_Enable, CLK, MBR_Enable, OUT_Enable, PC_Enable;
  wire [1:0] B_Select;
  wire [2:0] ALU_Select;
  wire [4:0] MBR;
  wire [7:0] A_q, alu_1_out, B_q, Data, multiplexer_1_out, PC_q;
  wire [7:5] MBR_q;

  Register A (.D(alu_1_out), .en(A_Enable), .Q(A_q), .clk(CLK), .clr(RST));
  Register B (.D(alu_1_out), .en(B_Enable), .Q(B_q), .clk(CLK), .clr(RST));
  Register u_MBR (.D(Data), .en(MBR_Enable), .Q({MBR_q, MBR}), .clk(CLK), .clr(RST));
  Register PC (.D(alu_1_out), .en(PC_Enable), .Q(PC_q), .clk(CLK), .clr(RST));
  Register u_OUT (.D(alu_1_out), .en(OUT_Enable), .Q(Out), .clk(CLK), .clr(RST));
  Hex_Digit_Display hex_digit_display_1 (.value(Out[7:4]));  // open: dp
  Multiplexer #(.select(2), .width(8)) multiplexer_1 (
    .in0(B_q), .in1({MBR_q, MBR}), .in2(PC_q), .in3(Input), .out(multiplexer_1_out), .sel(B_Select));  // open: en
  Hex_Digit_Display hex_digit_display_2 (.value(Out[3:0]));  // open: dp
  ALU alu_1 (.A(A_q), .B(multiplexer_1_out), .Out(alu_1_out), .S(ALU_Select));  // open: ZF, VF
  Clock u_clk (.out(CLK));
  RAM #(.bus("asynch")) ram_1 (.addr(PC_q), .data(Data));  // open: sel, ld, clr
  control control_1 (
    .Rst(RST), .From_MBR(MBR), .CLK(CLK),
    .Write_Enables({A_Enable, B_Enable, MBR_Enable, PC_Enable, OUT_Enable}), .B_Select(B_Select),
    .ALU_Select(ALU_Select), .Halt(halt));

  // Other names for the same wires on the sheet: WE[4:0] = {A_Enable, B_Enable, MBR_Enable, PC_Enable, OUT_Enable}
endmodule

module control (
  input  Rst,
  input  [4:0] From_MBR,
  input  CLK,
  output [4:0] Write_Enables,
  output [1:0] B_Select,
  output [2:0] ALU_Select,
  output Halt
);

  wire DSP, not_1_out;
  wire [4:0] multiplexer_1_out, Next_State, SPC_q;
  wire [15:0] rom_1_data;

  Multiplexer #(.width(5)) multiplexer_1 (
    .in0(Next_State), .in1(From_MBR), .out(multiplexer_1_out), .sel(DSP));  // open: en
  Register #(.width(5)) SPC (.D(multiplexer_1_out), .Q(SPC_q), .clk(CLK), .clr(Rst));  // open: en
  ROM #(.addrWidth(5), .dataWidth(16)) rom_1 (.addr(SPC_q), .data(rom_1_data));  // open: sel
  Register #(.width(16), .trigger("falling")) IR (
    .D(rom_1_data), .Q({Next_State, DSP, ALU_Select, B_Select, Write_Enables}), .clk(CLK), .clr(Rst));  // open: en
  not not_1 (not_1_out, SPC_q[1]);
  and and_1 (Halt, SPC_q[0], not_1_out, SPC_q[2], SPC_q[3], SPC_q[4]);

  // Notes on the sheet:
  //   contents of rom_1 (hex, n*v repeats v):
  //   804 11c0 19c2 400 28e0 30f0 0 4000 4801 0 5800 60a4 68a2 0 7800 80a4 88b0 91c0 99c2 0 a900 b110 0
  //   c000 c808 0 da00 e210 0 1d00 1e02 1f02
endmodule
